# Fritzing sketch sketch (saved by Fritzing 0.9.4)

parts:
  Part1 = Arduino Nano (Rev3.0)
  WeMos_D1_Mini_OLED_Shield1 = WeMos D1 Mini OLED Shield
  IR1 = TSOP312.., 314.. [package=THT]

nets:
  N1: Part1.GND, WeMos_D1_Mini_OLED_Shield1.RST, IR1.Data
  N2: Part1.D8, IR1.GND
  N3: Part1.5V, WeMos_D1_Mini_OLED_Shield1.A0
  N4: Part1.A5, WeMos_D1_Mini_OLED_Shield1.D0
  N5: Part1.A4, WeMos_D1_Mini_OLED_Shield1.D5
